// Logisim project cpu.circ as structural Verilog: 1 circuit, main circuit main
module main (
  output [15:0] pc,
  output [7:0] A,
  output halt,
  output [7:0] B
);

  wire clock_1_out, clock_2_out, clock_3_out, clock_4_out, not_1_out, ROM_sel, undriven, undriven_2;
  wire [7:0] ctl, imm, memdata, ram_1_data;
  wire [15:0] adder_1_out, bit_extender_1_out, multiplexer_1_out;

  // Probe on pc
  // Probe on ctl
  // Probe on imm
  Multiplexer #(.width(16)) multiplexer_1 (
    .in0(16'h1), .in1(bit_extender_1_out), .out(multiplexer_1_out), .sel(ctl[0]), .en(1'b1));
  assign bit_extender_1_out = {{8{imm[7]}}, imm};  // Bit_Extender bit_extender_1
  // Probe on imm
  // Probe on memdata
  Adder #(.width(16)) adder_1 (.a(pc), .b(multiplexer_1_out), .out(adder_1_out));  // open: cin, cout
  // Probe on A
  // Probe on B
  Register #(.width(16)) u_PC (.D(adder_1_out), .Q(pc), .clk(clock_1_out));  // open: en, clr
  Clock clock_1 (.out(clock_1_out));
  rom ROM (.A(pc), .sel(ROM_sel), .D({imm, ctl}));
  // Probe on {imm, ctl}
  Comparator #(.width(16), .mode("unsigned")) comparator_1 (.a({imm, ctl}), .b(16'h1), .eq(halt));  // open: gt, lt
  Clock clock_2 (.out(clock_2_out));
  not not_1 (not_1_out, 1'b0);
  RAM #(.bus("asynch")) ram_1 (.addr(imm), .data(ram_1_data), .sel(1'b1), .ld(not_1_out));  // open: clr
  Multiplexer #(.width(8)) multiplexer_2 (.in0(ram_1_data), .in1(imm), .out(memdata), .sel(ctl[4]));  // open: en
  Register register_1 (.D(memdata), .en(ctl[2]), .Q(A), .clk(clock_3_out), .clr(undriven));
  Clock clock_3 (.out(clock_3_out));
  Register register_2 (.D(memdata), .en(ctl[3]), .Q(B), .clk(clock_4_out), .clr(undriven_2));
  Clock clock_4 (.out(clock_4_out));
  // also tied to VCC on the sheet: ROM_sel

  // Other names for the same wires on the sheet: ctl_jmp = ctl[0]; insn[15:0] = {imm, ctl}; ctl_wra = ctl[2];
  //   ctl_wrb = ctl[3]; ctl_ldmem_ldimm = ctl[4]; memaddr[7:0] = imm
endmodule
